# Fritzing sketch LedStrip (saved by Fritzing 0.9.2b)
breadboards: 1

parts:
  JACK1 = 2.1mm Barrel Jack with Terminal Block [part_number=5V]
  C2 = Electrolytic Capacitor [capacitance=1000µF voltage=10V package="300 mil [THT, electrolytic]"]
  R1 = Resistor [tolerance=±5% resistance=470 package=THT]
  NEOPIXEL1 = Neopixel Strip -- White (30/m)
  Part1 = Arduino Uno (Rev3)

nets:
  N1: JACK1.POS, C2.+, NEOPIXEL1.+5V
  GND: JACK1.NEG, C2.-, NEOPIXEL1.GND, Part1.GND
  N2: R1.Pin_0, Part1.D2
  N3: R1.Pin_1, NEOPIXEL1.Din

custom parts:
  Neopixel Strip -- White (30/m): These NeoPixel strips have 30 digitally-addressable pixel LEDs per meter and are very affordable and are only 12.5 mm wide, 10 mm if you remove the strip from the casing.
