# Fritzing sketch PanAndTilt (saved by Fritzing 0.9.2b)

parts:
  Part2 = Arduino Uno (Rev3)
  J1 = Basic Servo
  J3 = Basic Servo
  PWM1 = PCA9685 16x12-bit PWM Breakout
  JACK1 = 2.1mm Barrel Jack with Terminal Block

nets:
  N1: Part2.A4/SDA, PWM1.no_name_yet#504
  N2: Part2.A5/SCL, PWM1.no_name_yet#503
  N3: Part2.5V, PWM1.no_name_yet#505
  N4: Part2.GND, PWM1.no_name_yet#501, PWM1.no_name_yet#701, PWM1.no_name_yet#1000, PWM1.no_name_yet#1001, JACK1.NEG
  N5: J1.pulse, PWM1.no_name_yet#0
  N6: J3.pulse, PWM1.no_name_yet#1
  N7: PWM1.no_name_yet#100, PWM1.no_name_yet#101, PWM1.no_name_yet#706, JACK1.POS

notes:
  TILT
  PAN
