# Fritzing sketch Diagrama (saved by Fritzing 0.9.2b)
breadboards: 1

parts:
  S1 = Pushbutton [package="[THT]"]
  S2 = Pushbutton [package="[THT]"]
  part = Rotary Potentiometer (Large) [maximum_resistance=5kΩ package=THT]
  part_2 = Rotary Potentiometer (Large) [maximum_resistance=5kΩ package=THT]
  part_3 = Resistor [tolerance=±5% resistance=10k package=THT]
  part_4 = Resistor [tolerance=±5% resistance=10k package=THT]
  Grove1 = Grove OLED 128x96
  Part3 = Arduino Nano (Rev3.0) (ICSP)

nets:
  N1: S1.Pin_1, S1.Pin_2, part_3.Pin_1, Part3.D11/MOSI
  VCC: S1.Pin_3, S1.Pin_4, S2.Pin_3, S2.Pin_4, part.leg1, part_2.leg1, Grove1.VCC, Part3.5V
  N2: S2.Pin_1, S2.Pin_2, part_4.Pin_1, Part3.D10
  N3: part.wiper, Part3.A6
  GND: part.leg2, part_2.leg2, part_3.Pin_0, part_4.Pin_0, Grove1.GND, Part3.GND
  N4: part_2.wiper, Part3.A0
  N5: Grove1.SDA, Part3.A4
  N6: Grove1.SCL, Part3.A5
